# Fritzing sketch sketch (saved by Fritzing 0.9.3b)
breadboards: 2

parts:
  U1 = ESP8266 NodeMCU LoLin module
  J1 = Basic Servo
  J5 = Basic Servo
  J6 = Basic Servo
  J7 = Basic Servo
  YF-S201_Flow_Meter1 = YF-S201 Water Flow Meter
  Water_Level_Sensor1 = Water Level Sensor

nets:
  N1: U1.D0, J1.pulse
  N2: U1.D3, J5.pulse
  N3: U1.D5, J6.pulse
  N4: U1.D6, J7.pulse
  N5: U1.D7, YF-S201_Flow_Meter1.SIG
  N6: U1.A0, Water_Level_Sensor1.SIG
  GND: J7.gnd, YF-S201_Flow_Meter1.GND, Water_Level_Sensor1.GND
  VCC: J7.vcc, YF-S201_Flow_Meter1.VCC, Water_Level_Sensor1.VCC

notes:
  Main gate
  Gate 1
  Gate 2
  Gate3
  Power Supply
  5v
  GND

custom parts:
  ESP8266 NodeMCU LoLin module: ESP8266 based NodeMCU
  YF-S201 Water Flow Meter: The YF-S201 Flow Meter. The input voltage is 5V to 24V (DC).
  Water Level Sensor: A water level sensor. This sensor operates at 3V to 5V. The Sig (signal) pin outputs an analogue signal that is in proportion to the amount of water in contact with the sensor.
